# Fritzing sketch dooropener (saved by Fritzing 0.9.2b)
circuit board: 5.61529cm x 5.82723cm
breadboards: 1

parts:
  U1 = atmega328 [package=dip]
  U2 = Voltage Regulator - 5V [package="DPak [SMD]"]
  C1 = Electrolytic Capacitor [capacitance=10μF package="0605 [SMD, electrolytic]"]
  C2 = Electrolytic Capacitor [capacitance=10μF package="0605 [SMD, electrolytic]"]
  LED2 = LED - 5mm [color="Red (633nm)" package="5 mm [THT]"]
  R2 = Resistor [tolerance=±5% resistance=220 package=THT]
  R3 = Resistor [tolerance=±5% resistance=10k package="0603 [SMD]"]
  C3 = Ceramic Capacitor [capacitance=22pF package="100 mil [THT, multilayer]"]
  C4 = Ceramic Capacitor [capacitance=22pF package="100 mil [THT, multilayer]"]
  XTAL1 = CRYSTAL - kHz [frequency="16 MHz"]
  S1 = Momentary Switch [package=ksa_sealed_tac_switch]
  IC1 = L293D [package=THT]
  J1 = Screw terminal - 2 pins [package=THT]
  J2 = Screw terminal - 2 pins [package=THT]
  J3 = Screw terminal - 2 pins [package=THT]

nets:
  N1: U1.RESET, R3.Pin_1, S1.2
  N2: U1.D0_(RX), IC1.In_1
  N3: U1.D1_(TX), IC1.In_2
  N4: U1.D2, IC1.In_3
  N5: U1.D3_(PWM), IC1.In_4
  N6: U1.VCC, U1.AVCC, U1.AREF, U2.input_voltage, U2.output_voltage, C1.+, C2.+, R2.Pin_0, R3.Pin_0, IC1.Enable_1, IC1.Enable_2, IC1.+V, J3.pin2
  GND: U1.GND, U2.GND, C1.-, C2.-, LED2.cathode, C3.0, C4.0, S1.4, IC1.0V, J3.pin1
  N7: U1.XLAT1, C4.1, XTAL1.pin_0
  N8: U1.XLAT2, C3.1, XTAL1.pin_1
  N9: LED2.anode, R2.Pin_1
  N10: IC1.Out_1_(_Controlled_by_Enable_1_), J2.pin2
  N11: IC1.Out_2_(_Controlled_by_Enable_1_), J2.pin1
  N12: IC1.Out_3_(_Controlled_by_Enable_2_), J1.pin2
  N13: IC1.Out_4_(_Controlled_by_Enable_2_), J1.pin1
