# Fritzing sketch dooropener3 (saved by Fritzing 0.8.5b)
circuit board: 5.93488cm x 4.3819cm

parts:
  S1 = Toggle Switch [package=THT]
  Vin+- = Screw terminal - 2 pins [package=THT]
  C1 = Electrolytic Capacitor [capacitance=10µF package="100 mil [THT, electrolytic]"]
  LED = LED - 3mm [color="Red (633nm)" package="3 mm [THT]"]
  XTAL = CRYSTAL - kHz [frequency="16 MHz"]
  C3 = Ceramic Capacitor [capacitance=22pF package="100 mil [THT, multilayer]"]
  C4 = Ceramic Capacitor [capacitance=22pF package="100 mil [THT, multilayer]"]
  C5 = Electrolytic Capacitor [capacitance=10µF package="100 mil [THT, electrolytic]"]
  5v = Voltage Regulator [package=to220-igo]
  A4988 = A4988 Stepper Motor Driver Carrier
  M1 = Screw terminal - 2 pins [package=THT]
  M2 = Screw terminal - 2 pins [package=THT]
  C6 = Electrolytic Capacitor [capacitance=1µF package="100 mil [THT, electrolytic]"]
  3_3v = Voltage Regulator - 3.3V [package="TO220 [THT]"]
  RC522 = RFID-RC522-v2
  ATMEGA168 = atmega168 [package=dip]
  C7 = Electrolytic Capacitor [capacitance=10µF package="100 mil [THT, electrolytic]"]
  R_RX_TX = Header 3 [package=jst-3-pth]
  330 = Resistor [tolerance=±5% resistance=330 package=THT]
  C2 = Electrolytic Capacitor [capacitance=10µF package="100 mil [THT, electrolytic]"]
  10k = Resistor [tolerance=±5% resistance=10k package=THT]
  MVin-+ = screw terminal, 2 pins

nets:
  GND: S1.L1, Vin+-.pin1, C1.-, LED.cathode, C3.1, C4.0, 5v.GND, A4988.GROUND#147, 3_3v.GND, RC522.GND, ATMEGA168.GND, C7.-, C2.-
  N1: S1.COM, C5.+, ATMEGA168.RESET
  N2: S1.L2, 10k.Pin_1
  N3: Vin+-.pin2, C1.+, 5v.IN, 3_3v.input_voltage
  N4: LED.anode, 330.Pin_1
  N5: XTAL.pin_0, C3.0, ATMEGA168.XLAT1
  N6: XTAL.pin_1, C4.1, ATMEGA168.XLAT2
  N7: C5.-, R_RX_TX.1
  VDD: 5v.OUT, A4988.VDD, ATMEGA168.VCC, ATMEGA168.AVCC, ATMEGA168.AREF, 330.Pin_0, C2.+, 10k.Pin_0
  N8: A4988.Enable, ATMEGA168.D2
  N9: A4988.RESET, A4988.SLEEP
  N10: A4988.STEP, ATMEGA168.D3_(PWM)
  N11: A4988.DIR, ATMEGA168.D4
  N12: A4988.VMOT, C6.+, MVin-+.pin1
  N13: A4988.GROUND#141, C6.-, MVin-+.pin2
  N14: A4988.OUT_2B, M1.pin1
  N15: A4988.OUT_2A, M1.pin2
  N16: A4988.OUT_1A, M2.pin1
  N17: A4988.OUT_1B, M2.pin2
  N18: 3_3v.output_voltage, RC522.3_3V, C7.+
  N19: RC522.SDA, ATMEGA168.D10_(PWM)
  N20: RC522.SCK, ATMEGA168.D13
  N21: RC522.MOSI, ATMEGA168.D11_(PWM)
  N22: RC522.MISO, ATMEGA168.D12
  N23: RC522.RST, ATMEGA168.D9_(PWM)
  N24: ATMEGA168.D0_(RX), R_RX_TX.2
  N25: ATMEGA168.D1_(TX), R_RX_TX.3

custom parts:
  RFID-RC522-v2: A simple China made RFID-RC522 Reader; do check the pin labels, as this is a MFRC522 based clone.
