# Fritzing sketch dooroperner2 (saved by Fritzing 0.9.2b)
circuit board: 5.4cm x 4cm
breadboards: 1

parts:
  Motor_Driver = L293D [package=THT]
  OUT_3&4 = Screw terminal - 2 pins [package=THT]
  OUT_1&2 = Screw terminal - 2 pins [package=THT]
  12V_In = Screw terminal - 2 pins [package=THT]
  U1 = Voltage Regulator - 5V [package="TO220 [THT]"]
  R1 = Resistor [tolerance=±5% resistance=10k package=THT]
  XTAL1 = Crystal [frequency="16 Mhz" package=THT]
  C3 = Ceramic Capacitor [capacitance=22pF package="100 mil [THT, multilayer]"]
  C4 = Ceramic Capacitor [capacitance=22pF package="100 mil [THT, multilayer]"]
  JP1 = Header 6 [package=1x06-smd]
  JP2 = Header 6 [package=1x06-smd]
  JP3 = Header 6 [package=1x06-smd]
  LED1 = LED - 3mm [color="Red (633nm)" package="3 mm [THT]"]
  R2 = Resistor [tolerance=±5% resistance=330 package="1206 [SMD]"]
  C5 = Electrolytic Capacitor [capacitance=10μF package="0605 [SMD, electrolytic]"]
  C6 = Electrolytic Capacitor [capacitance=10μF package="0605 [SMD, electrolytic]"]
  S2 = Toggle Switch [package=THT]
  U2 = atmega328 [package=dip]
  MD09B1 = A4988 Stepper Motor Driver Carrier  # not connected

nets:
  N1: Motor_Driver.Enable_1, Motor_Driver.Enable_2, Motor_Driver.+V, 12V_In.pin1, U1.input_voltage, C6.+
  N2: Motor_Driver.In_1, U2.D5_(PWM)
  N3: Motor_Driver.Out_1_(_Controlled_by_Enable_1_), Motor_Driver.Out_2_(_Controlled_by_Enable_1_), OUT_1&2.pin1, OUT_1&2.pin2
  GND: Motor_Driver.0V, 12V_In.pin2, U1.GND, C3.1, C4.1, JP2.1, R2.Pin_1, C5.-, C6.-, S2.L1, U2.GND
  N4: Motor_Driver.In_2, U2.D6_(PWM)
  N5: Motor_Driver.In_3, U2.D7
  N6: Motor_Driver.Out_3_(_Controlled_by_Enable_2_), OUT_3&4.pin2
  N7: Motor_Driver.Out_4_(_Controlled_by_Enable_2_), OUT_3&4.pin1
  N8: Motor_Driver.In_4, U2.D8
  N9: U1.output_voltage, R1.Pin_0, JP3.1, LED1.anode, C5.+, U2.VCC, U2.AVCC, U2.AREF
  N10: R1.Pin_1, S2.COM, U2.RESET
  N11: XTAL1.pin_0, C3.0, U2.XLAT1
  N12: XTAL1.pin_1, C4.0, U2.XLAT2
  N13: JP1.1, U2.A5
  N14: JP1.2, U2.A4
  N15: JP1.3, U2.A3
  N16: JP1.4, U2.A2
  N17: JP1.5, U2.A1
  N18: JP1.6, U2.A0
  N19: JP2.2, U2.D13
  N20: JP2.3, U2.D12
  N21: JP2.4, U2.D11_(PWM)
  N22: JP2.5, U2.D10_(PWM)
  N23: JP2.6, U2.D9_(PWM)
  N24: JP3.2, U2.D0_(RX)
  N25: JP3.3, U2.D1_(TX)
  N26: JP3.4, U2.D2
  N27: JP3.5, U2.D3_(PWM)
  N28: JP3.6, U2.D4
  N29: LED1.cathode, R2.Pin_0
